# Fritzing sketch MODELAGEM (saved by Fritzing 0.9.2b)
breadboards: 1

parts:
  Componente2 = SRF05 Ultrasonic Rangefinder
  Componente4 = SRF05 Ultrasonic Rangefinder
  Componente5 = SRF05 Ultrasonic Rangefinder
  Componente6 = Arduino Nano (Rev3.0)
  Part1 = KY-006 Passive Buzzer Module [package="Breakout board"]
  U1 = LIPO-1000mAh [package=lipo-1000]  # not connected

nets:
  VCC: Componente2.VCC, Componente4.VCC, Componente5.VCC, Componente6.5V, Part1.-
  N1: Componente2.Trig, Componente4.Trig, Componente5.Trig, Componente6.D8
  N2: Componente2.Echo, Componente6.D10
  GND: Componente2.GND, Componente4.GND, Componente5.GND, Componente6.GND, Part1.S
  N3: Componente4.Echo, Componente6.D11/MOSI
  N4: Componente5.Echo, Componente6.D12/MISO

custom parts:
  KY-006 Passive Buzzer Module: Passive Piezoelectric Buzzer Module Keyes KY-006, it can produce a range of sound tones depending on the input frequency.
